// Logisim project alu.circ as structural Verilog: 1 circuit, main circuit alu
module alu (
  input  [31:0] A,
  input  [31:0] B,
  input  [3:0] ALUSel,
  output [31:0] Result
);

  wire A_compare, B_compare, comparator_3_lt, comparator_4_lt, comparator_5_lt, comparator_6_lt,
       comparator_7_lt;
  wire [15:0] A_Lower_16, A_Lower_16_opp, B_Lower_16, B_Lower_16_opp, p1_lower_16, p1_lower_16_opp,
       p2_lower_16, p2_lower_16_opp;
  wire [31:0] A_Lower_32, A_Lower_32_opp, A_Upper_32, A_Upper_32_opp, add, adder_1_out, adder_2_out,
       adder_4_out, adder_5_out, adder_6_out, adder_7_out, adder_9_out, adder_10_out, adder_11_out,
       adder_12_out, and1, B_Lower_32, B_Lower_32_opp, B_Upper_32, B_Upper_32_opp, divu, intermediate_1,
       intermediate_1_opp, intermediate_2, intermediate_2_opp, mulh, mulh_neg_neg, mulh_neg_positive,
       mulh_positive_neg, mulhu, mult, multiplexer_1_out, multiplexer_2_out, not_1_out, not_2_out, or1, p0,
       p0_opp, p1, p1_lower_32, p1_lower_32_opp, p1_opp, p2, p2_lower_32, p2_lower_32_opp, p2_opp, p3,
       p3_opp, remu, shifter_1_out, shifter_5_out, shifter_6_out, shifter_10_out, shifter_12_out,
       shifter_13_out, sll1, slt, sra1, srl1, sub, subtractor_2_out, subtractor_4_out, summer_1,
       summer_1_opp, u_mul_hi, u_mul_hi_opp, xor1;

  // Probe on mulh_neg_positive
  // Probe on mulh_neg_neg
  // Probe on mulh_positive_neg
  // Probe on mulhu
  assign not_1_out = ~A;  // NOT_Gate not_1, 32 bits wide
  assign not_2_out = ~B;  // NOT_Gate not_2, 32 bits wide
  Multiplexer #(.width(32), .enable("false")) multiplexer_1 (
    .in0(mulh_neg_neg), .in1(mulh_neg_positive), .out(multiplexer_1_out), .sel(B_compare));
  Multiplexer #(.width(32), .enable("false")) multiplexer_2 (
    .in0(mulh_positive_neg), .in1(mulhu), .out(multiplexer_2_out), .sel(B_compare));
  Adder #(.width(32)) adder_1 (.a(32'h1), .b(not_1_out), .out(adder_1_out));  // open: cin, cout
  Adder #(.width(32)) adder_2 (.a(not_2_out), .b(32'h1), .out(adder_2_out));  // open: cin, cout
  Comparator #(.width(32)) comparator_1 (.a(B), .b({32{1'b0}}), .gt(B_compare));  // open: eq, lt
  Comparator #(.width(32)) comparator_2 (.a(A), .b({32{1'b0}}), .gt(A_compare));  // open: eq, lt
  // Probe on p1_lower_32
  // Probe on p3
  Multiplexer #(.width(32), .enable("false")) multiplexer_3 (
    .in0(multiplexer_1_out), .in1(multiplexer_2_out), .out(mulh), .sel(A_compare));
  Multiplier #(.width(32)) multiplier_1 (.a(adder_1_out), .b(adder_2_out), .cout(mulh_neg_neg));  // open: out, cin
  Bit_Extender #(.in_width(32)) bit_extender_1 (.in(p1), .out(p1_lower_16));
  assign p1_lower_32 = {{16{1'b0}}, p1_lower_16};  // Bit_Extender bit_extender_2
  Shifter #(.width(32), .shift("lr")) shifter_1 (.in(p2), .\dist (5'b10000), .out(shifter_1_out));
  Adder #(.width(32)) adder_3 (.a(A), .b(B), .out(add));  // open: cin, cout
  assign and1 = A & B;  // AND_Gate and_1, 32 bits wide
  assign or1 = A | B;  // OR_Gate or_1, 32 bits wide
  assign xor1 = A ^ B;  // XOR_Gate xor_1, 32 bits wide
  Shifter #(.width(32), .shift("lr")) shifter_2 (.in(A), .\dist (B[4:0]), .out(srl1));
  Shifter #(.width(32), .shift("ar")) shifter_3 (.in(A), .\dist (B[4:0]), .out(sra1));
  Bit_Extender #(.in_width(32)) bit_extender_3 (.in(A), .out(A_Lower_16));
  assign A_Lower_32 = {{16{1'b0}}, A_Lower_16};  // Bit_Extender bit_extender_4
  Shifter #(.width(32), .shift("lr")) shifter_4 (.in(A), .\dist (5'b10000), .out(A_Upper_32));
  // Probe on p0
  Multiplier #(.width(32)) multiplier_2 (.a(B_Lower_32), .b(A_Lower_32), .out(p0));  // open: cin, cout
  Multiplier #(.width(32)) multiplier_3 (.a(B_Upper_32), .b(A_Upper_32), .out(p3));  // open: cin, cout
  // Probe on shifter_5_out
  Shifter #(.width(32), .shift("lr")) shifter_5 (.in(p0), .\dist (5'b10000), .out(shifter_5_out));
  Bit_Extender #(.in_width(32)) bit_extender_5 (.in(p2), .out(p2_lower_16));
  assign p2_lower_32 = {{16{1'b0}}, p2_lower_16};  // Bit_Extender bit_extender_6
  // Probe on p2_lower_32
  Adder #(.width(32)) adder_4 (.a(p3), .b(shifter_1_out), .out(adder_4_out));  // open: cin, cout
  Shifter #(.width(32), .shift("lr")) shifter_6 (.in(p1), .\dist (5'b10000), .out(shifter_6_out));
  // Probe on adder_5_out
  Adder #(.width(32)) adder_5 (.a(shifter_5_out), .b(p1_lower_32), .out(adder_5_out));  // open: cin, cout
  Adder #(.width(32)) adder_6 (.a(adder_4_out), .b(shifter_6_out), .out(adder_6_out));  // open: cin, cout
  Shifter #(.width(32)) shifter_7 (.in(A), .\dist (B[4:0]), .out(sll1));
  Comparator #(.width(32)) comparator_3 (.a(A), .b(B), .lt(comparator_3_lt));  // open: gt, eq
  Divider #(.width(32)) divider_1 (.a(A), .b(B), .out(divu));  // open: upper, rem
  Divider #(.width(32)) divider_2 (.a(A), .b(B), .rem(remu));  // open: out, upper
  Multiplier #(.width(32)) multiplier_4 (.a(A), .b(B), .out(mult));  // open: cin, cout
  Multiplier #(.width(32)) multiplier_5 (.a(A), .b(B), .cout(mulhu));  // open: out, cin
  Subtractor #(.width(32)) subtractor_1 (.a(A), .b(B), .out(sub));  // open: bin, bout
  // Probe on p1
  Adder #(.width(32)) adder_7 (.a(adder_5_out), .b(p2_lower_32), .out(adder_7_out));  // open: cin, cout
  Adder #(.width(32)) adder_8 (.a(adder_6_out), .b(summer_1), .out(u_mul_hi));  // open: cin, cout
  assign slt = {{31{1'b0}}, comparator_3_lt};  // Bit_Extender bit_extender_7
  Bit_Extender #(.in_width(32)) bit_extender_8 (.in(B), .out(B_Lower_16));
  assign B_Lower_32 = {{16{1'b0}}, B_Lower_16};  // Bit_Extender bit_extender_9
  Shifter #(.width(32), .shift("lr")) shifter_8 (.in(B), .\dist (5'b10000), .out(B_Upper_32));
  Multiplier #(.width(32)) multiplier_6 (.a(B_Upper_32), .b(A_Lower_32), .out(p1));  // open: cin, cout
  Multiplier #(.width(32)) multiplier_7 (.a(A_Upper_32), .b(B_Lower_32), .out(p2));  // open: cin, cout
  Shifter #(.width(32), .shift("lr")) shifter_9 (.in(adder_7_out), .\dist (5'b10000), .out(summer_1));
  // Probe on p1_lower_32_opp
  Bit_Extender #(.in_width(32)) bit_extender_10 (.in(p1_opp), .out(p1_lower_16_opp));
  assign p1_lower_32_opp = {{16{1'b0}}, p1_lower_16_opp};  // Bit_Extender bit_extender_11
  // Probe on p3_opp
  Shifter #(.width(32), .shift("lr")) shifter_10 (.in(p2_opp), .\dist (5'b10000), .out(shifter_10_out));
  Subtractor #(.width(32)) subtractor_2 (
    .a(intermediate_1), .b(intermediate_2), .out(subtractor_2_out));  // open: bin, bout
  Bit_Extender #(.in_width(32)) bit_extender_12 (.in(B), .out(A_Lower_16_opp));
  assign A_Lower_32_opp = {{16{1'b0}}, A_Lower_16_opp};  // Bit_Extender bit_extender_13
  Shifter #(.width(32), .shift("lr")) shifter_11 (.in(B), .\dist (5'b10000), .out(A_Upper_32_opp));
  Multiplier #(.width(32)) multiplier_8 (.a(B_Lower_32_opp), .b(A_Lower_32_opp), .out(p0_opp));  // open: cin, cout
  Multiplier #(.width(32)) multiplier_9 (.a(B_Upper_32_opp), .b(A_Upper_32_opp), .out(p3_opp));  // open: cin, cout
  // Probe on shifter_12_out
  Shifter #(.width(32), .shift("lr")) shifter_12 (.in(p0_opp), .\dist (5'b10000), .out(shifter_12_out));
  // Probe on p2_lower_32_opp
  Adder #(.width(32)) adder_9 (.a(p3_opp), .b(shifter_10_out), .out(adder_9_out));  // open: cin, cout
  Subtractor #(.width(32)) subtractor_3 (
    .a(u_mul_hi), .b(subtractor_2_out), .out(mulh_neg_positive));  // open: bin, bout
  Multiplexer #(.width(32), .enable("false")) multiplexer_4 (
    .in0({32{1'b0}}), .in1(B), .out(intermediate_1), .sel(comparator_4_lt));
  Comparator #(.width(32)) comparator_4 (.a(A), .b({32{1'b0}}), .lt(comparator_4_lt));  // open: gt, eq
  Multiplexer #(.width(32), .enable("false")) multiplexer_5 (
    .in0({32{1'b0}}), .in1(A), .out(intermediate_2), .sel(comparator_5_lt));
  Comparator #(.width(32)) comparator_5 (.a(B), .b({32{1'b0}}), .lt(comparator_5_lt));  // open: gt, eq
  // Probe on p0_opp
  Bit_Extender #(.in_width(32)) bit_extender_14 (.in(p2_opp), .out(p2_lower_16_opp));
  assign p2_lower_32_opp = {{16{1'b0}}, p2_lower_16_opp};  // Bit_Extender bit_extender_15
  Adder #(.width(32)) adder_10 (.a(adder_9_out), .b(shifter_13_out), .out(adder_10_out));  // open: cin, cout
  Shifter #(.width(32), .shift("lr")) shifter_13 (.in(p1_opp), .\dist (5'b10000), .out(shifter_13_out));
  Multiplexer #(.select(4), .width(32), .enable("false")) multiplexer_6 (
    .in0(add), .in1(and1), .in2(or1), .in3(xor1), .in4(srl1), .in5(sra1), .in6(sll1), .in7(slt), .in8(divu),
    .in9(remu), .in10(mult), .in11(mulhu), .in12(sub), .in13(B), .in14(mulh), .out(Result), .sel(ALUSel));  // open: in15
  BitAdder bitadder_1 ();  // open: in0, out
  // Probe on intermediate_1
  // Probe on intermediate_2
  // Probe on p1_opp
  // Probe on adder_11_out
  Adder #(.width(32)) adder_11 (.a(shifter_12_out), .b(p1_lower_32_opp), .out(adder_11_out));  // open: cin, cout
  Multiplier #(.width(32)) multiplier_10 (.a(B_Upper_32_opp), .b(A_Lower_32_opp), .out(p1_opp));  // open: cin, cout
  Multiplier #(.width(32)) multiplier_11 (.a(A_Upper_32_opp), .b(B_Lower_32_opp), .out(p2_opp));  // open: cin, cout
  Adder #(.width(32)) adder_12 (.a(adder_11_out), .b(p2_lower_32_opp), .out(adder_12_out));  // open: cin, cout
  Shifter #(.width(32), .shift("lr")) shifter_14 (.in(adder_12_out), .\dist (5'b10000), .out(summer_1_opp));
  Adder #(.width(32)) adder_13 (.a(adder_10_out), .b(summer_1_opp), .out(u_mul_hi_opp));  // open: cin, cout
  Bit_Extender #(.in_width(32)) bit_extender_16 (.in(A), .out(B_Lower_16_opp));
  assign B_Lower_32_opp = {{16{1'b0}}, B_Lower_16_opp};  // Bit_Extender bit_extender_17
  Shifter #(.width(32), .shift("lr")) shifter_15 (.in(A), .\dist (5'b10000), .out(B_Upper_32_opp));
  Subtractor #(.width(32)) subtractor_4 (
    .a(intermediate_1_opp), .b(intermediate_2_opp), .out(subtractor_4_out));  // open: bin, bout
  Comparator #(.width(32)) comparator_6 (.a(A), .b({32{1'b0}}), .lt(comparator_6_lt));  // open: gt, eq
  Comparator #(.width(32)) comparator_7 (.a(B), .b({32{1'b0}}), .lt(comparator_7_lt));  // open: gt, eq
  Subtractor #(.width(32)) subtractor_5 (
    .a(u_mul_hi_opp), .b(subtractor_4_out), .out(mulh_positive_neg));  // open: bin, bout
  // Probe on intermediate_2_opp
  Multiplexer #(.width(32), .enable("false")) multiplexer_7 (
    .in0({32{1'b0}}), .in1(B), .out(intermediate_2_opp), .sel(comparator_6_lt));
  // Probe on intermediate_1_opp
  Multiplexer #(.width(32), .enable("false")) multiplexer_8 (
    .in0({32{1'b0}}), .in1(A), .out(intermediate_1_opp), .sel(comparator_7_lt));

  // Other names for the same wires on the sheet: bsel[31:0] = B; shifted[4:0] = B[4:0]

  // Notes on the sheet:
  //   INPUTS to your circuit
  //   DON'T CHANGE THE LOCATIONS OF THE INPUTS AND OUTPUTS!
  //   OUTPUT from your circuit
endmodule
