// Logisim project cpu.circ as structural Verilog: 4 circuits, main circuit main
module main (
  input  [31:0] INSTRUCTION,
  input  CLOCK,
  output [31:0] FETCH_ADDRESS,
  output [31:0] ra,
  output [31:0] sp,
  output [31:0] t0,
  output [31:0] t1,
  output [31:0] t2,
  output [31:0] s0,
  output [31:0] s1,
  output [31:0] a0
);

  wire and_1_out, and_2_out, ASel, B_J_Select, Branch_Result, BrEq, BrLT, BrUn, BSel, comparator_1_eq,
       comparator_2_eq, comparator_3_eq, comparator_4_eq, comparator_5_eq, comparator_6_eq, comparator_7_eq,
       comparator_8_eq, comparator_9_eq, comparator_10_eq, DMEM_p1, DMEM_p2, J_Select, MemRW, or_1_out,
       or_4_out, PCSel, RegWEn;
  wire [1:0] and_3_out, rem_load;
  wire [2:0] F3, ImmSel;
  wire [3:0] ALUSel, WBSel;
  wire [6:0] F7, OPCODE;
  wire [7:0] multiplexer_9_out;
  wire [15:0] multiplexer_10_out, undriven;
  wire [24:7] P_INST;
  wire [31:0] A_In, ALU_Result, ALU_Result_Non_Load, B_In, div_load, divider_2_out, divider_3_rem, IMM_OUT,
       IMM_OUT_INT, Incremented_PC, load_base_address, load_byte_result, load_hw_result, Mem_Result,
       multiplexer_1_out, multiplier_1_out, PC_q, Pre_Mem_Result, R1, R2, R_Pipeline, subtractor_1_out,
       WB_Result;

  Adder #(.width(32)) adder_1 (.a(PC_q), .b(32'h4), .out(Incremented_PC));  // open: cin, cout
  Multiplexer #(.width(32), .enable("false")) multiplexer_1 (
    .in0(Incremented_PC), .in1(ALU_Result), .out(multiplexer_1_out), .sel(or_1_out));
  or or_1 (or_1_out, PCSel, B_J_Select);
  Comparator #(.width(7)) comparator_1 (.a(OPCODE), .b(7'b1101111), .eq(comparator_1_eq));  // open: gt, lt
  Comparator #(.width(7)) comparator_2 (.a(OPCODE), .b(7'b1100111), .eq(comparator_2_eq));  // open: gt, lt
  Register #(.width(32)) PC (.D(multiplexer_1_out), .clk(CLOCK), .Q(PC_q));  // open: en, clr
  immediate_generator immediate_generator_1 (
    .Imm_Sel(ImmSel), .P_Inst({F7, P_INST[24:15], F3, P_INST[11:7], OPCODE}), .Immediate(IMM_OUT_INT));
  or or_2 (J_Select, comparator_1_eq, comparator_2_eq);
  Divider #(.width(32)) divider_1 (.a(PC_q), .b(32'h4), .out(FETCH_ADDRESS));  // open: upper, rem
  Register #(.width(32)) register_1 (
    .D(R_Pipeline), .clk(CLOCK), .Q({F7, P_INST[24:15], F3, P_INST[11:7], OPCODE}));  // open: en, clr
  Multiplexer #(.width(32), .enable("false")) multiplexer_2 (
    .in0(INSTRUCTION), .in1(32'h13), .out(R_Pipeline), .sel(Branch_Result));
  Multiplexer #(.width(32), .enable("false")) multiplexer_3 (.in0(R2), .in1(IMM_OUT), .out(B_In), .sel(BSel));
  or or_3 (B_J_Select, Branch_Result, J_Select);
  Divider #(.width(32)) divider_2 (.a(IMM_OUT_INT), .b(32'h4), .out(divider_2_out));  // open: upper, rem
  Multiplier #(.width(32)) multiplier_1 (.a(FETCH_ADDRESS), .b(32'h4), .out(multiplier_1_out));  // open: cin, cout
  Multiplexer #(.width(32), .enable("false")) multiplexer_4 (
    .in0(IMM_OUT_INT), .in1(IMM_OUT_INT), .out(IMM_OUT), .sel(ASel));
  Subtractor #(.width(32)) subtractor_1 (.a(multiplier_1_out), .b(32'h4), .out(subtractor_1_out));  // open: bin, bout
  control control_1 (
    .P_Inst({F7, P_INST[24:15], F3, P_INST[11:7], OPCODE}), .BrEq(BrEq), .ALUSel(ALUSel), .BrLT(BrLT),
    .MemRW(MemRW), .PCSel(PCSel), .RegWEn(RegWEn), .ImmSel(ImmSel), .WBSel(WBSel), .BrUn(BrUn), .ASel(ASel),
    .BSel(BSel));
  Multiplexer #(.width(32), .enable("false")) multiplexer_5 (.in0(R1), .in1(subtractor_1_out), .out(A_In), .sel(ASel));
  regfile_main RegFile (
    .rs2(P_INST[24:20]), .rd(P_INST[11:7]), .Read_Data_1(R1), .Read_Data_2(R2), .ra(ra), .sp(sp), .t0(t0),
    .t1(t1), .t2(t2), .s0(s0), .s1(s1), .a0(a0), .rs1(P_INST[19:15]), .Write_Data(WB_Result),
    .RegWEn(RegWEn), .clk(CLOCK));
  Comparator #(.width(7)) comparator_3 (.a(OPCODE), .b(7'b0000011), .eq(comparator_3_eq));  // open: gt, lt
  Comparator #(.width(3)) comparator_4 (.a(F3), .b(3'b000), .eq(comparator_4_eq));  // open: gt, lt
  Comparator #(.width(7)) comparator_5 (.a(OPCODE), .b(7'b0000011), .eq(comparator_5_eq));  // open: gt, lt
  Comparator #(.width(3)) comparator_6 (.a(F3), .b(3'b001), .eq(comparator_6_eq));  // open: gt, lt
  Divider #(.width(32)) divider_3 (.a(B_In), .b(32'h4), .out(div_load), .rem(divider_3_rem));  // open: upper
  Bit_Extender #(.in_width(32), .out_width(2)) bit_extender_1 (.in(divider_3_rem), .out(rem_load));
  alu Arithmetic_Logic_Unit (.A(A_In), .B(B_In), .ALUSel(ALUSel), .Result(ALU_Result_Non_Load));
  and and_1 (and_1_out, comparator_3_eq, comparator_4_eq);
  and and_2 (and_2_out, comparator_5_eq, comparator_6_eq);
  branch_control branch_control_1 (
    .R1(R1), .R2(R2), .Beq(BrEq), .Blt(BrLT), .BrUn(BrUn), .OPCODE(OPCODE), .Branch_Result(Branch_Result));
  Multiplexer #(.width(32), .enable("false")) multiplexer_6 (
    .in0(ALU_Result_Non_Load), .in1(load_base_address), .out(ALU_Result), .sel(or_4_out));
  or or_4 (or_4_out, and_1_out, and_2_out);
  Multiplier #(.width(32)) multiplier_2 (.a(div_load), .b(32'h4), .out(load_base_address));  // open: cin, cout
  // mem_main DMEM: pin names not known; wires that end beside it: DMEM_p1, DMEM_p2, ALU_Result, R2, MemRW, CLOCK, Pre_Mem_Result
  Comparator #(.width(7)) comparator_7 (.a(OPCODE), .b(7'b0000011), .eq(comparator_7_eq));  // open: gt, lt
  Comparator #(.width(7)) comparator_8 (.a(OPCODE), .b(7'b0000011), .eq(comparator_8_eq));  // open: gt, lt
  Comparator #(.width(3)) comparator_9 (.a(F3), .b(3'b000), .eq(comparator_9_eq));  // open: gt, lt
  Comparator #(.width(3)) comparator_10 (.a(F3), .b(3'b001), .eq(comparator_10_eq));  // open: gt, lt
  Multiplexer #(.select(4), .width(32), .enable("false")) multiplexer_7 (
    .in1(ALU_Result), .in2(Mem_Result), .in3(Incremented_PC), .out(WB_Result), .sel(WBSel));  // open: in0, in4, in5, in6, in7, in8, in9, in10, in11, in12, in13, in14, in15
  and and_3 (and_3_out[0], comparator_7_eq, comparator_9_eq);
  and and_4 (and_3_out[1], comparator_8_eq, comparator_10_eq);
  Multiplexer #(.select(2), .width(32), .enable("false")) multiplexer_8 (
    .in0(Pre_Mem_Result), .in1(load_byte_result), .in2(load_hw_result), .out(Mem_Result), .sel(and_3_out));  // open: in3
  Multiplexer #(.select(2), .width(8), .enable("false")) multiplexer_9 (
    .in0(Pre_Mem_Result[7:0]), .in1(Pre_Mem_Result[15:8]), .in2(Pre_Mem_Result[23:16]),
    .in3(Pre_Mem_Result[31:24]), .out(multiplexer_9_out), .sel(rem_load));
  Multiplexer #(.select(2), .width(16), .enable("false")) multiplexer_10 (
    .in0(Pre_Mem_Result[15:0]), .in2(Pre_Mem_Result[31:16]), .in3(undriven), .out(multiplexer_10_out),
    .sel(rem_load));  // open: in1
  assign load_byte_result = {{24{multiplexer_9_out[7]}}, multiplexer_9_out};  // Bit_Extender bit_extender_2
  assign load_hw_result = {{16{multiplexer_10_out[15]}}, multiplexer_10_out};  // Bit_Extender bit_extender_3

  // Other names for the same wires on the sheet: clk = CLOCK; fetch_addr[31:0] = FETCH_ADDRESS;
  //   P_INST (some bits) = {F7, F3, OPCODE}; rd[4:0] = P_INST[11:7]; rs1[4:0] = P_INST[19:15];
  //   rs2[4:0] = P_INST[24:20]

  // Notes on the sheet:
  //   Output
  //   Inputs/Outputs from run.circ. DO NOT MOVE THESE.
  //   Inputs
  //   Inputs/Outputs from run.circ. DO NOT MOVE THESE.
endmodule

module immediate_generator (
  input  [2:0] Imm_Sel,
  input  [31:0] P_Inst,
  output [31:0] Immediate
);

  wire and_1_out, and_2_out, comparator_1_eq, comparator_2_eq, comparator_3_eq, comparator_4_eq, or_1_out;
  wire [31:0] B_Result, I_Result, J_Result, normal_I, S_Result, special_I;

  assign normal_I = {{20{P_Inst[31]}}, P_Inst[31:20]};  // Bit_Extender bit_extender_1
  Multiplexer #(.select(3), .width(32), .enable("false")) multiplexer_1 (
    .in1(I_Result), .in2(S_Result), .in3(B_Result), .in4(J_Result), .in5({P_Inst[31:12], {12{1'b0}}}),
    .out(Immediate), .sel(Imm_Sel));  // open: in0, in6, in7
  assign special_I = {{27{P_Inst[24]}}, P_Inst[24:20]};  // Bit_Extender bit_extender_2
  assign B_Result = {{19{P_Inst[31]}}, {P_Inst[31], P_Inst[7], P_Inst[30:25], P_Inst[11:8], 1'b0}};  // Bit_Extender bit_extender_3
  assign J_Result = {{11{P_Inst[31]}}, {P_Inst[31], P_Inst[19:12], P_Inst[20], P_Inst[30:21], 1'b0}};  // Bit_Extender bit_extender_4
  Comparator #(.width(7)) comparator_1 (.a(P_Inst[6:0]), .b(7'b0010011), .eq(comparator_1_eq));  // open: gt, lt
  Comparator #(.width(3)) comparator_2 (.a(Imm_Sel), .b(3'b001), .eq(comparator_2_eq));  // open: gt, lt
  Comparator #(.width(3)) comparator_3 (.a(P_Inst[14:12]), .b(3'b001), .eq(comparator_3_eq));  // open: gt, lt
  Comparator #(.width(3)) comparator_4 (.a(P_Inst[14:12]), .b(3'b101), .eq(comparator_4_eq));  // open: gt, lt
  and and_1 (and_1_out, comparator_2_eq, comparator_1_eq);
  or or_1 (or_1_out, comparator_3_eq, comparator_4_eq);
  assign S_Result = {{20{P_Inst[31]}}, {P_Inst[31:25], P_Inst[11:7]}};  // Bit_Extender bit_extender_5
  and and_2 (and_2_out, and_1_out, or_1_out);
  Multiplexer #(.width(32), .enable("false")) multiplexer_2 (
    .in0(normal_I), .in1(special_I), .out(I_Result), .sel(and_2_out));

  // Other names for the same wires on the sheet: B_11 = P_Inst[7]; OPCODE[6:0] = P_Inst[6:0];
  //   FUNCT_3_IMM[2:0] = P_Inst[14:12]; J_12[7:0] = P_Inst[19:12]; U_Result[31:12] = P_Inst[31:12];
  //   I_Intermediate[11:0] = P_Inst[31:20]; J_11 = P_Inst[20]; J_1_10[9:0] = P_Inst[30:21];
  //   FUNCT_7_IMM[6:0] = P_Inst[31:25]
endmodule

module control (
  input  [31:0] P_Inst,
  output BrEq,
  output [3:0] ALUSel,
  output BrLT,
  output MemRW,
  output PCSel,
  output RegWEn,
  output [2:0] ImmSel,
  output [3:0] WBSel,
  output BrUn,
  output ASel,
  output BSel
);

  wire comparator_1_eq, comparator_2_eq, comparator_3_eq, or_1_out;
  wire [2:0] FUNCT_3;
  wire [6:0] FUNCT_7;

  ROM #(.addrWidth(17), .dataWidth(19)) rom_1 (
    .addr({P_Inst[6:0], FUNCT_3, FUNCT_7}),
    .data({BrEq, BrLT, PCSel, ImmSel, BrUn, ASel, BSel, ALUSel, MemRW, RegWEn, WBSel}));
  Comparator #(.width(7), .mode("unsigned")) comparator_1 (
    .a(P_Inst[6:0]), .b(7'b0110011), .eq(comparator_1_eq));  // open: gt, lt
  // Probe on {BrEq, BrLT, PCSel, ImmSel, BrUn, ASel, BSel, ALUSel, MemRW, RegWEn, WBSel}
  // Probe on FUNCT_7
  Multiplexer #(.width(7), .enable("false")) multiplexer_1 (
    .in0({7{1'b0}}), .in1(P_Inst[31:25]), .out(FUNCT_7), .sel(comparator_1_eq));
  // Probe on WBSel
  // Probe on BrEq
  Comparator #(.width(7), .mode("unsigned")) comparator_2 (
    .a(P_Inst[6:0]), .b(7'b0110111), .eq(comparator_2_eq));  // open: gt, lt
  Comparator #(.width(7), .mode("unsigned")) comparator_3 (
    .a(P_Inst[6:0]), .b(7'b1101111), .eq(comparator_3_eq));  // open: gt, lt
  Multiplexer #(.width(3), .enable("false")) multiplexer_2 (
    .in0(P_Inst[14:12]), .in1(3'b000), .out(FUNCT_3), .sel(or_1_out));
  or or_1 (or_1_out, comparator_2_eq, comparator_3_eq);

  // Other names for the same wires on the sheet: control_word[18:0] = {BrEq, BrLT, PCSel, ImmSel, BrUn, ASel, BSel, ALUSel, MemRW, RegWEn, WBSel};
  //   O_37[16:0] = {P_Inst[6:0], FUNCT_3, FUNCT_7}; OPCODE[6:0] = P_Inst[6:0]; FUNCT_3_IMM[2:0] = P_Inst[14:12]

  // Notes on the sheet:
  //   contents of rom_1 (hex, n*v repeats v):
  //   3072*0 2412 127*0 2412 127*0 2412 16127*0 2411 127*0 2591 127*0 25d1 255*0 24d1 127*0 2511 31*0 2551
  //   95*0 2491 127*0 2451 15743*0 4420 16127*0 11 291 30*0 311 95*0 191 391 126*0 1d1 128*0 2d1 126*0 d1
  //   127*0 111 211 126*0 91 127*0 51 251 3198*0 a411 45055*0 46c00 127*0 6c00 383*0 26c00 255*0 27c00
  //   3327*0 2413 8191*0 8c13
endmodule

module branch_control (
  input  [31:0] R1,
  input  [31:0] R2,
  input  Beq,
  input  Blt,
  input  BrUn,
  input  [6:0] OPCODE,
  output Branch_Result
);

  wire branch_check, comparator_5_eq, eq_result, lt_signed_result, lt_unsigned_result, neq_result;

  Comparator #(.width(7)) comparator_1 (.a(OPCODE), .b(7'b1100011), .eq(branch_check));  // open: gt, lt
  Comparator #(.width(32), .mode("unsigned")) comparator_2 (.a(R1), .b(R2), .lt(lt_unsigned_result));  // open: gt, eq
  Comparator #(.width(32)) comparator_3 (.a(R1), .b(R2), .lt(lt_signed_result));  // open: gt, eq
  Comparator #(.width(32)) comparator_4 (.a(R1), .b(R2), .eq(eq_result));  // open: gt, lt
  Comparator #(.width(32)) comparator_5 (.a(R1), .b(R2), .eq(comparator_5_eq));  // open: gt, lt
  not not_1 (neq_result, comparator_5_eq);
  Multiplexer #(.select(4), .enable("false")) multiplexer_1 (
    .in0(1'b0), .in1(1'b0), .in2(1'b0), .in3(1'b0), .in4(1'b0), .in5(1'b0), .in6(1'b0), .in7(1'b0),
    .in8(neq_result), .in9(eq_result), .in10(lt_unsigned_result), .in11(1'b0), .in12(1'b0), .in13(1'b0),
    .in14(lt_signed_result), .in15(1'b0), .out(Branch_Result), .sel({branch_check, BrUn, Blt, Beq}));

  // Other names for the same wires on the sheet: branch_selector[3:0] = {branch_check, BrUn, Blt, Beq}
endmodule
